# Fritzing sketch Fritzing scheme (saved by Fritzing 0.9.3b)
breadboards: 1

parts:
  IC1 = L293D [package=THT]
  VCC1 = 4 x AAA Battery Mount
  Part1 = Arduino Uno (Rev3) - ICSP
  HC-SR04_Sensor_1 = HC-SR04 Ultrasonic Distance Sensor
  HC-SR04_Sensor_3 = HC-SR04 Ultrasonic Distance Sensor
  M3 = DC Motor
  IR1 = TSOP312.., 314.. [package=THT]
  LED1 = smd LED [color="Green (560nm)" package="0805 [SMD]"]
  LED2 = smd LED [color="Blue (430nm)" package="0805 [SMD]"]
  R1 = Resistor [tolerance=±5% resistance=220 package="2010 [SMD]"]
  R2 = Resistor [tolerance=±5% resistance=220 package="2010 [SMD]"]
  VCC2 = Battery block 9V
  M2 = DC Motor
  HC-SR04_Sensor_2 = HC-SR04 Ultrasonic Distance Sensor

nets:
  N1: IC1.Enable_1, Part1.D5_PWM
  N2: IC1.In_1, Part1.D4
  N3: IC1.Out_1_(_Controlled_by_Enable_1_), M2.pin_1
  GND: IC1.0V, VCC1.-, Part1.GND, HC-SR04_Sensor_1.GND, IR1.Vs, LED1.anode, R1.Pin_1, VCC2.+, HC-SR04_Sensor_2.GND
  N4: IC1.Out_2_(_Controlled_by_Enable_1_), M2.pin_2
  N5: IC1.In_2, Part1.D3_PWM
  N6: IC1.+Vmotor, VCC1.+
  N7: IC1.Enable_2, Part1.D6_PWM
  N8: IC1.In_3, Part1.D7
  N9: IC1.Out_3_(_Controlled_by_Enable_2_), M3.pin_2
  N10: IC1.Out_4_(_Controlled_by_Enable_2_), M3.pin_1
  N11: IC1.In_4, Part1.D8
  VCC: IC1.+V, Part1.5V, HC-SR04_Sensor_1.VCC, HC-SR04_Sensor_3.VCC, IR1.Data, VCC2.-, HC-SR04_Sensor_2.VCC
  N12: Part1.A0, HC-SR04_Sensor_2.ECHO
  N13: Part1.A1, HC-SR04_Sensor_1.ECHO
  N14: Part1.A2, IR1.GND
  N15: Part1.A3, HC-SR04_Sensor_3.ECHO
  N16: Part1.A4/SDA, R2.Pin_1
  N17: Part1.D9_PWM, HC-SR04_Sensor_3.TRIG
  N18: Part1.D10_PWM/SS, HC-SR04_Sensor_2.TRIG
  N19: Part1.D11_PWM/MOSI, HC-SR04_Sensor_1.TRIG
  N20: Part1.D12/MISO, LED2.cathode
